// Logisim project F.circ as structural Verilog: 1 circuit, main circuit main
module main (
);

  wire and_1_out, clock_1_out, j_k_ff_1_qn, or_1_out, or_2_out, or_3_out, or_4_out;
  wire [3:0] j_k_ff_1_q;

  and and_1 (and_1_out, j_k_ff_1_qn, or_1_out);
  or or_1 (or_1_out, j_k_ff_1_q[1], j_k_ff_1_q[2], j_k_ff_1_q[3]);
  or or_2 (or_2_out, j_k_ff_1_q[1], j_k_ff_1_q[2], j_k_ff_1_q[3]);
  or or_3 (or_3_out, j_k_ff_1_q[2], j_k_ff_1_q[3]);
  Clock clock_1 (.out(clock_1_out));
  or or_4 (or_4_out, j_k_ff_1_q[3], j_k_ff_1_q[2]);
  J_K_Flip_Flop j_k_ff_1 (
    .J(or_2_out), .clk(clock_1_out), .K(and_1_out), .Q(j_k_ff_1_q[0]), .Qn(j_k_ff_1_qn));  // open: preset, en, reset
  J_K_Flip_Flop j_k_ff_2 (
    .J(or_3_out), .clk(clock_1_out), .K(or_4_out), .Q(j_k_ff_1_q[1]));  // open: Qn, preset, en, reset
  J_K_Flip_Flop j_k_ff_3 (
    .J(j_k_ff_1_q[3]), .clk(clock_1_out), .K(j_k_ff_1_q[3]), .Q(j_k_ff_1_q[2]));  // open: Qn, preset, en, reset
  J_K_Flip_Flop j_k_ff_4 (.J(1'b1), .clk(clock_1_out), .K(1'b1), .Q(j_k_ff_1_q[3]));  // open: Qn, preset, en, reset
  Hex_Digit_Display hex_digit_display_1 (.value(j_k_ff_1_q));  // open: dp
endmodule
