// Logisim project CompuertasBasicas.circ as structural Verilog: 4 circuits, main circuit main
module AND (
  input  P,
  input  Q,
  output P_Q
);

  Transistor #(.\type ("n")) transistor_1 (.in(P), .out(P_Q), .gate(Q));
  Transistor transistor_2 (.in(P), .out(P_Q), .gate(1'b0));
endmodule

module main (
);

  AND and_1 ();  // open: P, Q, P_Q
endmodule

module NOT (
  input  P,
  output nP
);

  Transistor #(.\type ("n")) transistor_1 (.in(1'b0), .out(nP), .gate(P));
  Transistor transistor_2 (.in(1'b1), .out(nP), .gate(P));
endmodule

module OR (
  input  P,
  input  Q,
  output P_Q
);

  Transistor transistor_1 (.in(Q), .out(P_Q), .gate(P));
  Transistor transistor_2 (.in(P), .out(P_Q), .gate(Q));
  Transistor #(.\type ("n")) transistor_3 (.in(1'b1), .out(P_Q), .gate(Q));
endmodule
