// Logisim project Prueba.circ as structural Verilog: 1 circuit, main circuit main
module main (
);

  wire clock_1_out, j_k_ff_2_qn, not_1_out;
  wire [1:0] j_k_ff_2_q;

  Clock clock_1 (.out(clock_1_out));
  J_K_Flip_Flop j_k_ff_1 (
    .J(j_k_ff_2_q[0]), .clk(clock_1_out), .K(j_k_ff_2_q[0]), .Q(j_k_ff_2_q[1]));  // open: Qn, preset, en, reset
  J_K_Flip_Flop j_k_ff_2 (
    .J(j_k_ff_2_qn), .clk(clock_1_out), .K(not_1_out), .Q(j_k_ff_2_q[0]), .Qn(j_k_ff_2_qn));  // open: preset, en, reset
  not not_1 (not_1_out, 1'b0);
  Hex_Digit_Display hex_digit_display_1 (.value({2'b00, j_k_ff_2_q}));  // open: dp
endmodule
